# Fritzing sketch RFID Raspberry Pi (saved by Fritzing 0.9.3b)
breadboards: 1

parts:
  Raspberry_Pi_1 = Raspberry Pi 3 [part_number=RPI-3-V1.2]
  Componente1 = RFID-RC522-v2

nets:
  3V3: Raspberry_Pi_1.3v3, Componente1.3.3V
  GND: Raspberry_Pi_1.GPIO3, Raspberry_Pi_1.GND, Componente1.GND
  N1: Raspberry_Pi_1.GIPO10, Componente1.MOSI
  N2: Raspberry_Pi_1.GIPO9, Componente1.MISO
  N3: Raspberry_Pi_1.GIPO11, Componente1.SCK
  N4: Raspberry_Pi_1.GIPO8, Componente1.SDA
  N5: Raspberry_Pi_1.GIPO25, Componente1.RST

custom parts:
  RFID-RC522-v2: A simple China made RFID-RC522 Reader; do check the pin labels, as this is a MFRC522 based clone.
